// Digital circuit BF_Engine_1.dig as structural Verilog
module BF_Engine_1 (
  input  in_1,
  input  clk,
  input  plus,
  input  in_4
);

  wire _0_out, _1_out, _2_out, _3_out, _4_out, _5_out, _6_out, _7_out, _8_out, _9_out, _74173_4_pin11,
       _74173_4_pin12, _74173_4_pin13, _74173_4_pin14, _74193_1_pin12, _74193_1_pin13, _74193_2_pin12,
       _74193_2_pin13, _74193_3_pin12, _74193_3_pin13, _74193_5_pin1, _74193_5_pin9, _74193_5_pin10,
       _74193_5_pin12, _74193_5_pin13, _74193_5_pin15, _74193_6_pin1, _74193_6_pin9, _74193_6_pin10,
       _74193_6_pin15, _74540_1_pin11, _74540_1_pin12, _74540_1_pin13, _74540_1_pin14, _74540_1_pin15,
       _74540_1_pin16, _74540_1_pin17, A0, A1, A2, A3, A4, A5, A6, A7, A8, A9, A10, A11, A12, A13, A14, A15,
       A_out, Address_out, ALU, ALU_to_RAM_out, B_out, BUS0, BUS1, BUS2, BUS3, BUS4, BUS5, BUS6, BUS7, C_out,
       Clear_out, D_out, Dec_out, Deposit_nWR_out, diodebackward_1_out, diodebackward_2_out,
       diodebackward_5_out, diodebackward_10_out, diodebackward_14_out, diodebackward_31_out,
       diodebackward_46_out, DN, E_out, Examine_nRD_out, F_out, Inc_out, LDC, M0, M1, M2, M3, M4, M5, M6, M7,
       nALB, nDE, nLATCH, nLD, nOE, not_9_out, nWE, pullup_3_out, pullup_4_out, pullup_7_out, pullup_8_out,
       pullup_10_out, pullup_11_out, Q0, Q1, Q2, Q3, Q4, Q5, Q6, Q7, Q8, Q9, Q10, Q11, Q12, Q13, Q14, Q15,
       RES, UP;

  DiodeBackward diodebackward_1 (.in(Address_out), .out(diodebackward_1_out));
  PullUp pullup_1 (.out(diodebackward_1_out));
  DiodeBackward diodebackward_2 (.in(Dec_out), .out(diodebackward_2_out));
  not not_1 (nLD, _74540_1_pin11);
  PullUp pullup_2 (.out(diodebackward_2_out));
  PullUp pullup_3 (.out(pullup_3_out));
  DiodeBackward diodebackward_3 (.in(Inc_out), .out(pullup_3_out));
  _74139 _74139_1 (
    .pin1(1'b1), .pin2(1'b1), .pin3(1'b1), .pin8(1'b0), .pin11(nALB), .pin12(nDE), .pin13(1'b0), .pin14(ALU),
    .pin15(nWE), .pin16(1'b1));  // open: pin4, pin5, pin6, pin7, pin9, pin10
  PullUp pullup_4 (.out(pullup_4_out));
  DiodeBackward diodebackward_4 (.in(ALU_to_RAM_out), .out(pullup_4_out));
  DiodeBackward diodebackward_5 (.in(Examine_nRD_out), .out(diodebackward_5_out));
  DiodeBackward diodebackward_6 (.in(Examine_nRD_out), .out(pullup_4_out));
  DiodeBackward diodebackward_7 (.in(Deposit_nWR_out), .out(diodebackward_5_out));
  DiodeBackward diodebackward_8 (.in(Dec_out), .out(pullup_4_out));
  DiodeBackward diodebackward_9 (.in(Inc_out), .out(pullup_4_out));
  not not_2 (ALU, _74540_1_pin15);
  PullUp pullup_5 (.out(diodebackward_5_out));
  DiodeBackward diodebackward_10 (.in(ALU_to_RAM_out), .out(diodebackward_10_out));
  DiodeBackward diodebackward_11 (.in(Deposit_nWR_out), .out(diodebackward_10_out));
  not not_3 (LDC, _74540_1_pin17);
  not not_4 (nWE, _74540_1_pin16);
  nand nand_1 (UP, _74540_1_pin13, _74540_1_pin14);
  nand nand_2 (DN, _74540_1_pin12, _74540_1_pin14);
  PullUp pullup_6 (.out(diodebackward_10_out));
  PullUp pullup_7 (.out(pullup_7_out));
  DiodeBackward diodebackward_12 (.in(Examine_nRD_out), .out(pullup_7_out));
  PullUp pullup_8 (.out(pullup_8_out));
  DiodeBackward diodebackward_13 (.in(Clear_out), .out(pullup_8_out));
  _74540 _74540_1 (
    .pin1(1'b0), .pin2(pullup_8_out), .pin3(pullup_7_out), .pin4(diodebackward_10_out),
    .pin5(diodebackward_5_out), .pin6(pullup_4_out), .pin7(pullup_3_out), .pin8(diodebackward_2_out),
    .pin9(diodebackward_1_out), .pin10(1'b0), .pin11(_74540_1_pin11), .pin12(_74540_1_pin12),
    .pin13(_74540_1_pin13), .pin14(_74540_1_pin14), .pin15(_74540_1_pin15), .pin16(_74540_1_pin16),
    .pin17(_74540_1_pin17), .pin18(RES), .pin19(1'b0), .pin20(1'b1));
  Button #(.activeLow("true")) ALU_to_RAM (.out(ALU_to_RAM_out));
  Button #(.activeLow("true")) Clear (.out(Clear_out));
  Button #(.activeLow("true")) Examine_nRD (.out(Examine_nRD_out));
  Button #(.activeLow("true")) Deposit_nWR (.out(Deposit_nWR_out));
  Button #(.activeLow("true")) Dec (.out(Dec_out));
  Button #(.activeLow("true")) Inc (.out(Inc_out));
  Button #(.activeLow("true")) Address (.out(Address_out));
  nand nand_3 (nOE, LDC, in_1);
  _74173 _74173_1 (
    .pin1(1'b0), .pin2(1'b0), .pin3(A12), .pin4(A13), .pin5(A14), .pin6(A15), .pin7(nLATCH), .pin8(1'b0),
    .pin9(1'b0), .pin10(1'b0), .pin11(A11), .pin12(A10), .pin13(A9), .pin14(A8), .pin15(1'b0), .pin16(1'b1));
  Seven_Seg_Hex seven_seg_hex_1 (.d({A15, A14, A13, A12}), .dp(1'b0));
  Seven_Seg_Hex seven_seg_hex_2 (.d({A11, A10, A9, A8}), .dp(1'b0));
  Seven_Seg_Hex seven_seg_hex_3 (.d({A7, A6, A5, A4}), .dp(1'b0));
  _74173 _74173_2 (
    .pin1(1'b0), .pin2(1'b0), .pin3(A8), .pin4(A9), .pin5(A10), .pin6(A11), .pin7(nLATCH), .pin8(1'b0),
    .pin9(1'b0), .pin10(1'b0), .pin11(A7), .pin12(A6), .pin13(A5), .pin14(A4), .pin15(1'b0), .pin16(1'b1));
  Seven_Seg_Hex seven_seg_hex_4 (.d({A3, A2, A1, A0}), .dp(1'b0));
  Button #(.activeLow("true")) C (.out(C_out));
  Button #(.activeLow("true")) _8 (.out(_8_out));
  Button #(.activeLow("true")) _4 (.out(_4_out));
  Button #(.activeLow("true")) _0 (.out(_0_out));
  Button #(.activeLow("true")) D (.out(D_out));
  Button #(.activeLow("true")) _9 (.out(_9_out));
  Button #(.activeLow("true")) _5 (.out(_5_out));
  Button #(.activeLow("true")) _1 (.out(_1_out));
  Seven_Seg_Hex seven_seg_hex_5 (.d({Q15, Q14, Q13, Q12}), .dp(1'b0));
  Seven_Seg_Hex seven_seg_hex_6 (.d({Q11, Q10, Q9, Q8}), .dp(1'b0));
  Button #(.activeLow("true")) E (.out(E_out));
  Button #(.activeLow("true")) A (.out(A_out));
  Button #(.activeLow("true")) _6 (.out(_6_out));
  Button #(.activeLow("true")) _2 (.out(_2_out));
  _74173 _74173_3 (
    .pin1(1'b0), .pin2(1'b0), .pin3(A4), .pin4(A5), .pin5(A6), .pin6(A7), .pin7(nLATCH), .pin8(1'b0),
    .pin9(1'b0), .pin10(1'b0), .pin11(A3), .pin12(A2), .pin13(A1), .pin14(A0), .pin15(1'b0), .pin16(1'b1));
  Seven_Seg_Hex seven_seg_hex_7 (.d({Q7, Q6, Q5, Q4}), .dp(1'b0));
  Seven_Seg_Hex seven_seg_hex_8 (.d({Q3, Q2, Q1, Q0}), .dp(1'b0));
  Button #(.activeLow("true")) F (.out(F_out));
  Button #(.activeLow("true")) B (.out(B_out));
  Button #(.activeLow("true")) _7 (.out(_7_out));
  Button #(.activeLow("true")) _3 (.out(_3_out));
  _74173 _74173_4 (
    .pin1(1'b0), .pin2(1'b0), .pin3(A0), .pin4(A1), .pin5(A2), .pin6(A3), .pin7(nLATCH), .pin8(1'b0),
    .pin9(1'b0), .pin10(1'b0), .pin11(_74173_4_pin11), .pin12(_74173_4_pin12), .pin13(_74173_4_pin13),
    .pin14(_74173_4_pin14), .pin15(1'b0), .pin16(1'b1));
  Seven_Seg_Hex seven_seg_hex_9 (.d({M7, M6, M5, M4}), .dp(1'b0));
  DiodeBackward diodebackward_14 (.in(F_out), .out(diodebackward_14_out));
  DiodeBackward diodebackward_15 (.in(E_out), .out(diodebackward_14_out));
  DiodeBackward diodebackward_16 (.in(D_out), .out(diodebackward_14_out));
  DiodeBackward diodebackward_17 (.in(C_out), .out(diodebackward_14_out));
  DiodeBackward diodebackward_18 (.in(B_out), .out(diodebackward_14_out));
  DiodeBackward diodebackward_19 (.in(A_out), .out(diodebackward_14_out));
  DiodeBackward diodebackward_20 (.in(_9_out), .out(diodebackward_14_out));
  DiodeBackward diodebackward_21 (.in(_8_out), .out(diodebackward_14_out));
  Seven_Seg_Hex seven_seg_hex_10 (.d({M3, M2, M1, M0}), .dp(1'b0));
  PullUp pullup_9 (.out(diodebackward_14_out));
  PullUp pullup_10 (.out(pullup_10_out));
  DiodeBackward diodebackward_22 (.in(F_out), .out(pullup_10_out));
  DiodeBackward diodebackward_23 (.in(E_out), .out(pullup_10_out));
  DiodeBackward diodebackward_24 (.in(D_out), .out(pullup_10_out));
  DiodeBackward diodebackward_25 (.in(C_out), .out(pullup_10_out));
  DiodeBackward diodebackward_26 (.in(_7_out), .out(pullup_10_out));
  DiodeBackward diodebackward_27 (.in(_6_out), .out(pullup_10_out));
  DiodeBackward diodebackward_28 (.in(_5_out), .out(pullup_10_out));
  DiodeBackward diodebackward_29 (.in(_4_out), .out(pullup_10_out));
  not not_5 (_74173_4_pin12, pullup_10_out);
  not not_6 (_74173_4_pin11, diodebackward_14_out);
  PullUp pullup_11 (.out(pullup_11_out));
  DiodeBackward diodebackward_30 (.in(F_out), .out(pullup_11_out));
  DiodeBackward diodebackward_31 (.in(F_out), .out(diodebackward_31_out));
  DiodeBackward diodebackward_32 (.in(E_out), .out(pullup_11_out));
  DiodeBackward diodebackward_33 (.in(D_out), .out(diodebackward_31_out));
  DiodeBackward diodebackward_34 (.in(B_out), .out(pullup_11_out));
  DiodeBackward diodebackward_35 (.in(B_out), .out(diodebackward_31_out));
  DiodeBackward diodebackward_36 (.in(A_out), .out(pullup_11_out));
  DiodeBackward diodebackward_37 (.in(_9_out), .out(diodebackward_31_out));
  DiodeBackward diodebackward_38 (.in(_7_out), .out(pullup_11_out));
  DiodeBackward diodebackward_39 (.in(_7_out), .out(diodebackward_31_out));
  DiodeBackward diodebackward_40 (.in(_6_out), .out(pullup_11_out));
  DiodeBackward diodebackward_41 (.in(_5_out), .out(diodebackward_31_out));
  DiodeBackward diodebackward_42 (.in(_3_out), .out(pullup_11_out));
  DiodeBackward diodebackward_43 (.in(_3_out), .out(diodebackward_31_out));
  DiodeBackward diodebackward_44 (.in(_2_out), .out(pullup_11_out));
  DiodeBackward diodebackward_45 (.in(_1_out), .out(diodebackward_31_out));
  not not_7 (_74173_4_pin13, pullup_11_out);
  PullUp pullup_12 (.out(diodebackward_31_out));
  DiodeBackward diodebackward_46 (.in(F_out), .out(diodebackward_46_out));
  DiodeBackward diodebackward_47 (.in(E_out), .out(diodebackward_46_out));
  DiodeBackward diodebackward_48 (.in(D_out), .out(diodebackward_46_out));
  DiodeBackward diodebackward_49 (.in(C_out), .out(diodebackward_46_out));
  DiodeBackward diodebackward_50 (.in(B_out), .out(diodebackward_46_out));
  DiodeBackward diodebackward_51 (.in(A_out), .out(diodebackward_46_out));
  DiodeBackward diodebackward_52 (.in(_9_out), .out(diodebackward_46_out));
  DiodeBackward diodebackward_53 (.in(_8_out), .out(diodebackward_46_out));
  DiodeBackward diodebackward_54 (.in(_7_out), .out(diodebackward_46_out));
  DiodeBackward diodebackward_55 (.in(_6_out), .out(diodebackward_46_out));
  DiodeBackward diodebackward_56 (.in(_5_out), .out(diodebackward_46_out));
  DiodeBackward diodebackward_57 (.in(_4_out), .out(diodebackward_46_out));
  DiodeBackward diodebackward_58 (.in(_3_out), .out(diodebackward_46_out));
  DiodeBackward diodebackward_59 (.in(_2_out), .out(diodebackward_46_out));
  DiodeBackward diodebackward_60 (.in(_1_out), .out(diodebackward_46_out));
  DiodeBackward diodebackward_61 (.in(_0_out), .out(diodebackward_46_out));
  not not_8 (_74173_4_pin14, diodebackward_31_out);
  PullUp pullup_13 (.out(diodebackward_46_out));
  not not_9 (not_9_out, diodebackward_46_out);
  Monoflop monoflop_1 (.C(not_9_out), .R(1'b0), .nQ(nLATCH));  // open: Q
  Seven_Seg_Hex seven_seg_hex_11 (.d({BUS7, BUS6, BUS5, BUS4}), .dp(1'b0));
  Seven_Seg_Hex seven_seg_hex_12 (.d({BUS3, BUS2, BUS1, BUS0}), .dp(1'b0));
  LED led_1 (.in(nLATCH));
  _74193 _74193_1 (
    .pin1(A1), .pin2(Q1), .pin3(Q0), .pin4(DN), .pin5(UP), .pin6(Q2), .pin7(Q3), .pin8(1'b0), .pin9(A3),
    .pin10(A2), .pin11(nLD), .pin12(_74193_1_pin12), .pin13(_74193_1_pin13), .pin14(RES), .pin15(A0),
    .pin16(1'b1));
  _74193 _74193_2 (
    .pin1(A5), .pin2(Q5), .pin3(Q4), .pin4(_74193_1_pin13), .pin5(_74193_1_pin12), .pin6(Q6), .pin7(Q7),
    .pin8(1'b0), .pin9(A7), .pin10(A6), .pin11(nLD), .pin12(_74193_2_pin12), .pin13(_74193_2_pin13),
    .pin14(RES), .pin15(A4), .pin16(1'b1));
  _74193 _74193_3 (
    .pin1(A9), .pin2(Q9), .pin3(Q8), .pin4(_74193_2_pin13), .pin5(_74193_2_pin12), .pin6(Q10), .pin7(Q11),
    .pin8(1'b0), .pin9(A11), .pin10(A10), .pin11(nLD), .pin12(_74193_3_pin12), .pin13(_74193_3_pin13),
    .pin14(RES), .pin15(A8), .pin16(1'b1));
  _74193 _74193_4 (
    .pin1(A13), .pin2(Q13), .pin3(Q12), .pin4(_74193_3_pin13), .pin5(_74193_3_pin12), .pin6(Q14), .pin7(Q15),
    .pin8(1'b0), .pin9(A15), .pin10(A14), .pin11(nLD), .pin14(RES), .pin15(A12), .pin16(1'b1));  // open: pin12, pin13
  // _62256 _62256_1: pin names not known; wires that end beside it: Q14, Q12, Q7, Q6, Q5, Q4, Q3, Q2, Q1, Q0, BUS0, BUS1, BUS2, 1'b0, 1'b1, nWE, Q13, Q8, Q9, Q11, nOE, Q10, 1'b0, BUS7
  _74193 _74193_5 (
    .pin1(_74193_5_pin1), .pin2(M1), .pin3(M0), .pin4(in_4), .pin5(plus), .pin6(M2), .pin7(M3), .pin8(1'b0),
    .pin9(_74193_5_pin9), .pin10(_74193_5_pin10), .pin11(LDC), .pin12(_74193_5_pin12),
    .pin13(_74193_5_pin13), .pin14(RES), .pin15(_74193_5_pin15), .pin16(1'b1));
  _74193 _74193_6 (
    .pin1(_74193_6_pin1), .pin2(M5), .pin3(M4), .pin4(_74193_5_pin13), .pin5(_74193_5_pin12), .pin6(M6),
    .pin7(M7), .pin8(1'b0), .pin9(_74193_6_pin9), .pin10(_74193_6_pin10), .pin11(LDC), .pin14(RES),
    .pin15(_74193_6_pin15), .pin16(1'b1));  // open: pin12, pin13
  _74245 _74245_1 (
    .pin1(1'b0), .pin2(_74193_6_pin9), .pin3(_74193_6_pin10), .pin4(_74193_6_pin1), .pin5(_74193_6_pin15),
    .pin6(_74193_5_pin9), .pin7(_74193_5_pin10), .pin8(_74193_5_pin1), .pin9(_74193_5_pin15), .pin10(1'b0),
    .pin11(BUS0), .pin12(BUS1), .pin13(BUS2), .pin14(BUS3), .pin15(BUS4), .pin16(BUS5), .pin17(BUS6),
    .pin18(BUS7), .pin19(nDE), .pin20(1'b1));
  _74245 _74245_2 (
    .pin1(1'b1), .pin2(M7), .pin3(M6), .pin4(M5), .pin5(M4), .pin6(M3), .pin7(M2), .pin8(M1), .pin9(M0),
    .pin10(1'b0), .pin11(BUS0), .pin12(BUS1), .pin13(BUS2), .pin14(BUS3), .pin15(BUS4), .pin16(BUS5),
    .pin17(BUS6), .pin18(BUS7), .pin19(nDE), .pin20(1'b1));

  // Other names for the same wires on the sheet: DEC = in_4; INC = plus

  // Notes on the sheet:
  //   in_1: default 1
  //   clk: Hz: 10
  //   Front Panel
  //   UP
  //   LOAD
  //   DOWN
  //   COUNT
  //   WRITE
  //   ~DE
  //   READ
  //   RESET
  //   KEY DATA
  //   Hex Keypad
  //   KEYSWITCH REGISTER
  //   RAM ADDRESS
  //   M COUNT
  //   BUS DATA
  //   PC and RAM
  //   PROGRAM COUNTER
  //   RAM LO
  //   CELL INC/DEC
  //   DATA BUFFER LO
endmodule
